// Logisim project zadanie1.circ as structural Verilog: 1 circuit, main circuit Zadanie 1
module Zadanie_1 (
  input  a,
  input  b,
  input  c,
  input  d,
  output f__Shannon,
  output f__SOP,
  output zgodne__1___f_Shannon___f_SOP
);

  wire an, bn, cn, dn, f00, f01, f10, g0, g1, m3, m4, m5, m6, m7, m9, m12, m14, m15;

  not not_1 (an, a);
  not not_2 (bn, b);
  not not_3 (cn, c);
  not not_4 (dn, d);
  and and_1 (m3, an, bn, c, d);
  and and_2 (m4, an, b, cn, dn);
  and and_3 (m5, an, b, cn, d);
  and and_4 (f00, a, d);
  and and_5 (f01, an, d);
  or or_1 (f10, an, dn);
  xnor xnor_1 (zgodne__1___f_Shannon___f_SOP, f__Shannon, f__SOP);
  and and_6 (m6, an, b, c, dn);
  and and_7 (m7, an, b, c, d);
  and and_8 (m9, a, bn, cn, d);
  Multiplexer multiplexer_1 (.in0(f00), .in1(f01), .out(g0), .sel(c));  // open: en
  Multiplexer multiplexer_2 (.in0(f10), .in1(1'b1), .out(g1), .sel(c));  // open: en
  and and_9 (m12, a, b, cn, dn);
  and and_10 (m14, a, b, c, dn);
  and and_11 (m15, a, b, c, d);
  Multiplexer multiplexer_3 (.in0(g0), .in1(g1), .out(f__Shannon), .sel(b));  // open: en
  or or_2 (f__SOP, m3, m4, m5, m6, m7, m9, m12, m14, m15);

  // Other names for the same wires on the sheet: fS = f__Shannon; fSOP = f__SOP

  // Notes on the sheet:
  //   UKLAD PO ROZWINIECIU SHANNONA  f = b'(c'*f00 + c*f01) + b*(c'*f10 + c*f11)   ;   f00 = a*d,  f01 = a'*d,  f10 = a' + d',  f11 = 1
  //   ROWNOWAZNA SUMA MINTERMOW (SOP):  f = Sum m(3,4,5,6,7,9,12,14,15)
  //   WERYFIKACJA:  f(Shannon) XNOR f(SOP)  --  dla wszystkich 16 kombinacji a,b,c,d wyjscie 'zgodne' powinno wynosic 1
  //   POZIOM 2 (sterowanie c)
  //   POZIOM 1 (sterowanie b)
endmodule
